# Fritzing sketch Circuito (saved by Fritzing 1.0.4)
breadboards: 1

parts:
  Componente1 = Arduino Uno (Rev3)
  R1 = Resistor [tolerance=±5% power=0.25W resistance=220 package=THT]
  R2 = Resistor [tolerance=±5% power=0.25W resistance=220 package=THT]
  R3 = Resistor [tolerance=±5% power=0.25W resistance=220 package=THT]
  DHT1 = DHT11 Humitidy and Temperature Sensor (3 pins)
  e-radionica_com1 = LM393 LDR breakout [part_number=100027]
  J1 = Piezo Speaker
  LED1 = LED - 5mm [color="Red (633nm)" current=0.030A package="5 mm [THT]"]
  LED2 = LED - 5mm [color="Yellow (595nm)" current=0.030A package="5 mm [THT]"]
  LED3 = LED - 5mm [color="Green (555nm)" current=0.030A package="5 mm [THT]"]

nets:
  N1: Componente1.A0, e-radionica_com1.AO
  N2: Componente1.D8, LED3.anode
  N3: Componente1.D9_PWM, LED2.anode
  N4: Componente1.D10_PWM/SS, LED1.anode
  N5: Componente1.D11_PWM/MOSI, J1.pin2
  N6: Componente1.D2, DHT1.Signal
  5V: Componente1.5V, DHT1.Plus, e-radionica_com1.VCC
  GND: Componente1.GND, R1.Pin_0, R2.Pin_0, R3.Pin_0, DHT1.Gnd, e-radionica_com1.GND, J1.pin1
  N7: R1.Pin_1, LED1.cathode
  N8: R2.Pin_1, LED2.cathode
  N9: R3.Pin_1, LED3.cathode

custom parts:
  DHT11 Humitidy and Temperature Sensor (3 pins): DHT11 Humidity and Temperature Sensor (3 pins).
